// Logisim project cpu.circ as structural Verilog: 1 circuit, main circuit cpu
module cpu (
  input  clk,
  input  [31:0] INSTRUCTION,
  input  [31:0] READ_DATA,
  output [31:0] WRITE_ADDRESS,
  output [31:0] PROGRAM_COUNTER,
  output [31:0] ra,
  output [31:0] sp,
  output [31:0] t0,
  output [31:0] t1,
  output [31:0] t2,
  output [31:0] s0,
  output [31:0] s1,
  output [31:0] a0,
  output [31:0] tohost,
  output [3:0] WRITE_ENABLE,
  output [31:0] WRITE_DATA
);

  wire control_logic_1_regwen;
  wire [3:0] control_logic_1_alusel;
  wire [31:0] alu_out, IMM, InstFetch, PC4, regfile_1_read_data_1, WB_data;

  Adder #(.width(32)) adder_1 (.a(PROGRAM_COUNTER), .b(32'h4), .out(PC4));  // open: cin, cout
  Register #(.width(32)) PC (.D(PC4), .clk(clk), .Q(PROGRAM_COUNTER));  // open: en, clr
  Register #(.width(32)) register_1 (.D(INSTRUCTION), .en(1'b1), .clk(clk), .Q(InstFetch));  // open: clr
  imm_gen imm_gen_1 (.inst(InstFetch), .imm(IMM));  // open: ImmSel
  control_logic control_logic_1 (
    .RegWEn(control_logic_1_regwen), .ALUSel(control_logic_1_alusel), .inst(InstFetch));  // open: CSRWen, PCSel, ImmSel, BrUn, ASel, BSel, MemRW, WBSel, CSRSel, BrEq, BrLt
  regfile regfile_1 (
    .rs1(InstFetch[19:15]), .rd(InstFetch[11:7]), .Write_Data(WB_data), .RegWEn(control_logic_1_regwen),
    .clk(clk), .ra(ra), .sp(sp), .t0(t0), .t1(t1), .t2(t2), .s0(s0), .s1(s1), .a0(a0),
    .Read_Data_1(regfile_1_read_data_1));  // open: rs2, Read_Data_2
  alu alu_1 (.Result(alu_out), .A(regfile_1_read_data_1), .B(IMM), .ALUSel(control_logic_1_alusel));
  // branch_comp branch_comp_1: pin names not known
  Multiplexer #(.enable("false"), .select(2), .width(32)) multiplexer_1 (
    .in0(READ_DATA), .in1(alu_out), .in2(PC4), .out(WB_data), .sel(2'b01));  // open: in3
  csr csr_1 (.tohost(tohost));  // open: CSR_address, CSR_din, CSR_WE, clk

  // Notes on the sheet:
  //   Output to IMEM
  //   IMEM (do **NOT** move this)
  //   Inputs from IMEM
  //   Inputs/Outputs for testing. Do **NOT** move these.
  //   Outputs To DMEM
  //   DMEM (do **NOT** move this)
  //   Inputs From DMEM
endmodule
